# Fritzing sketch ESP01_NowSender (saved by Fritzing 0.9.9b)
breadboards: 1

parts:
  U1 = ESP8266 ESP-01 Upgraded WiFi Module [part_number=ESP8266]
  DHT1 = DHT22 Humidity and Temperature Sensor
  R2 = Resistor [tolerance=±5% power=0.25 resistance=10k package=THT]
  R1 = Resistor [tolerance=±5% resistance=10k power=0.25 package=THT]
  U2 = HT7333 [package="TO92 [THT]"]
  VCC1 = Battery block 9V
  C1_100µF = Capacitor Polarized [package=cpol-radial-10uf-25v]
  C2_100µF = Capacitor Polarized [package=cpol-radial-10uf-25v]
  C3 = Ceramic Capacitor [capacitance=100nF voltage=35V package="200 mil [THT, multilayer]"]

nets:
  VCC: U1.VCC, DHT1.VDD, R2.Pin_0, R1.Pin_0, U2.Vout, C2_100µF.+, C3.1
  N1: U1.GPIO_0, DHT1.DATA, R2.Pin_1
  N2: U1.CH_PD, R1.Pin_1
  GND: U1.GND, DHT1.GND, U2.GND, VCC1.-, C1_100µF.-, C2_100µF.-, C3.0
  N3: U2.Vin, VCC1.+, C1_100µF.+

custom parts:
  ESP8266 ESP-01 Upgraded WiFi Module: Upgraded Version ESP-01,all Flash are upgraded to 1M byte.Also support Cloud service remote transmission.
  HT7333: 3.3 V LDO linear regulator
