# Fritzing sketch NodeMCU_NowReceiver (saved by Fritzing 0.9.9b)
breadboards: 1

parts:
  U1 = NodeMCU V3.0
  LCD1 = TFT 1.8 inch 160x128 w SD

nets:
  N1: U1.D0, LCD1.pin_8
  N2: U1.D1, LCD1.pin_9
  N3: U1.D3, LCD1.pin4
  N4: U1.D4, LCD1.pin_5
  N5: U1.3V3, LCD1.pin_1
  N6: U1.GND#6, U1.GND#13, U1.GND#16, U1.GND#33, LCD1.pin2
  N7: U1.D5, LCD1.pin_7, LCD1.pin_12
  N8: U1.D6, LCD1.pin_11
  N9: U1.D7, LCD1.pin_6, LCD1.pin_10
  N10: U1.D8, LCD1.pin3

custom parts:
  NodeMCU V3.0: ESP8266 based NodeMCU
  TFT 1.8 inch 160x128 w SD: This is a generic 1.8 tft spi lcd display available on ebay and others. The 1.8" display has 128x160 color pixels.
